# Fritzing sketch Full_circuit (saved by Fritzing 1.0.6)
breadboards: 1

parts:
  M1 = Dagu DGServo 9g (Top view) [part_number=RS001B]  # not connected
  M2 = Dagu DGServo 9g (Top view) [part_number=RS001B]  # not connected
  M3 = Dagu DGServo 9g (Top view) [part_number=RS001B]  # not connected
  M4 = Dagu DGServo 9g (Top view) [part_number=RS001B]  # not connected
  Mod1 = Raspberry Pi 4B  # not connected
  M6 = gear-motor
  M7 = gear-motor
  M8 = gear-motor
  M9 = gear-motor
  HC-SR04_Sensor_2 = HC-SR04 Ultrasonic Distance Sensor
  HC-SR04_Sensor_3 = HC-SR04 Ultrasonic Distance Sensor
  HC-SR04_Sensor_4 = HC-SR04 Ultrasonic Distance Sensor
  HC-SR04_Sensor_5 = HC-SR04 Ultrasonic Distance Sensor
  S1 = H-Bridge with L298N
  S2 = H-Bridge with L298N
  Part2 = Adafruit PCA9685 PWM/Servo Breakout [part_number=815]
  Part1 = Arduino Mega 2560 (Rev3)
  VCC1 = 4 x AAA Battery Mount [internal_resistance=0.1Ω]
  M10 = RioRand LM2596
  CAMERA1 = TTL Serial JPEG Camera  # not connected

nets:
  N1: M6.pin_1, S2.M2-02
  N2: M6.pin_2, S2.M2-01
  N3: M7.pin_1, S1.M2-02
  N4: M7.pin_2, S1.M2-01
  N5: M8.pin_1, S2.M1-02
  N6: M8.pin_2, S2.M1-01
  N7: M9.pin_1, S1.M1-02
  N8: M9.pin_2, S1.M1-01
  VCC: HC-SR04_Sensor_2.VCC, HC-SR04_Sensor_3.VCC, HC-SR04_Sensor_4.VCC, HC-SR04_Sensor_5.VCC, Part2.VCC, Part1.5V
  N9: HC-SR04_Sensor_2.TRIG, Part1.D26
  N10: HC-SR04_Sensor_2.ECHO, Part1.D27
  GND: HC-SR04_Sensor_2.GND, HC-SR04_Sensor_3.GND, HC-SR04_Sensor_4.GND, HC-SR04_Sensor_5.GND, S1.GND, Part2.GND, Part1.GND, VCC1.-, M10.Pin_2, M10.Pin_4
  N11: HC-SR04_Sensor_3.TRIG, Part1.D24
  N12: HC-SR04_Sensor_3.ECHO, Part1.D25
  N13: HC-SR04_Sensor_4.TRIG, Part1.D22
  N14: HC-SR04_Sensor_4.ECHO, Part1.D23
  N15: HC-SR04_Sensor_5.TRIG, Part1.D28
  N16: HC-SR04_Sensor_5.ECHO, Part1.D29
  12V: S1.12V, S2.12V, Part1.VIN, VCC1.+, M10.Pin_1
  N17: S1.ENA, Part1.D7_PWM
  N18: S1.IN1, Part1.D34
  N19: S1.IN2, Part1.D35
  N20: S1.IN3, Part1.D36
  N21: S1.IN4, Part1.D37
  N22: S1.ENB, Part1.D8_PWM
  N23: S2.ENA, Part1.D5_PWM
  N24: S2.IN1, Part1.D30
  N25: S2.IN2, Part1.D31
  N26: S2.IN3, Part1.D32
  N27: S2.IN4, Part1.D33
  N28: S2.ENB, Part1.D6_PWM
  N29: Part2.PWRIN, M10.Pin_3
  N30: Part2.SDA, Part1.D20/SDA
  N31: Part2.SCL, Part1.D21/SCL

custom parts:
  H-Bridge with L298N: h-bridge
  Adafruit PCA9685 PWM/Servo Breakout: Using only two pins, control 16 free-running PWM outputs! I2C-controlled PWM driver with a built in clock. Unlike the TLC5940 family, you do not need to continuously send it signal tying up your microcontroller, its completely free running! 5V compliant, which means you can control it from a 3.3V microcontroller and still safely drive up to 6V outputs (this is good for when you want to control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
  TTL Serial JPEG Camera: TTL Serial JPEG Camera with NTSC Out
